# Fritzing sketch DataLogger_Schaltung (saved by Fritzing 0.9.2b)
breadboards: 1

parts:
  Raspberry_Pi1 = Raspberry Pi 2
  DHT1 = DHT11 Humitidy and Temperature Sensor  # not connected
  Bauteil1 = Adafruit I2C+SPI LCD Backpack [part_number="Adafruit #292"]
  U1 = LCD-16X2 [package=lcd-16x2_nosilk]
  R1 = Resistor [tolerance=±5% resistance=10k package="0603 [SMD]"]

nets:
  N1: Raspberry_Pi1.3v3, R1.Pin_1
  N2: Raspberry_Pi1.GPIO2, Bauteil1.DATA
  N3: Raspberry_Pi1.GPIO3, Bauteil1.CLOCK
  N4: Raspberry_Pi1.GPIO4, R1.Pin_0
  GND: Raspberry_Pi1.GND, Bauteil1.GND, U1.VSS, U1.R_W
  5V: Raspberry_Pi1.5V, Bauteil1.VCC, U1.VDD, U1.A
  N5: Bauteil1.CONTRAST, U1.VO
  N6: Bauteil1.RS, U1.RS
  N7: Bauteil1.E, U1.E
  N8: Bauteil1.DB0, U1.DB0
  N9: Bauteil1.DB1, U1.DB1
  N10: Bauteil1.DB2, U1.DB2
  N11: Bauteil1.DB3, U1.DB3
  N12: Bauteil1.DB4, U1.DB4
  N13: Bauteil1.DB5, U1.DB5
  N14: Bauteil1.DB6, U1.DB6
  N15: Bauteil1.DB7, U1.DB7
  N16: Bauteil1.LEDK, U1.K

custom parts:
  DHT11 Humitidy and Temperature Sensor: DHT11 Humidity and Temperature Sensor
  Adafruit I2C+SPI LCD Backpack: LCD backpacks reduce the number of pins needed to connect to an LCD. LCDs are a fun and easy way to have your microcontroller project talk back to you. Character LCDs are common, and easy to get, available in tons of colors and sizes. We've written tutorials on using character LCDs with an Arduino (or similar microcontroller) but find that the number of pins necessary to control the LCD can be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
